# Fritzing sketch circuit (saved by Fritzing 0.8.6b)
breadboards: 1

parts:
  Raspberry_Pi_A1 = Raspberry Pi A
  R1 = Resistor [tolerance=±5% resistance=10k package=THT]
  S1 = Round Pushbutton
  S2 = Round Pushbutton
  S3 = Round Pushbutton
  R2 = Resistor [tolerance=±5% resistance=10k package=THT]
  R3 = Resistor [tolerance=±5% resistance=10k package=THT]
  LED1 = LED - 5mm [color="Red (633nm)" package="5 mm [THT]"]
  LED2 = LED - 5mm [color="Red (633nm)" package="5 mm [THT]"]
  LED3 = LED - 5mm [color="Red (633nm)" package="5 mm [THT]"]
  S4 = SPST Switch [package=r_sw_th]  # not connected

nets:
  3V3: Raspberry_Pi_A1.3V3, Raspberry_Pi_A1.5V, S1.leg0, S2.leg0, S3.leg0
  N1: Raspberry_Pi_A1.GND, R1.Pin_1, R2.Pin_1, R3.Pin_1, LED1.cathode, LED2.cathode, LED3.cathode
  N2: Raspberry_Pi_A1.GPIO_23, LED2.anode
  N3: Raspberry_Pi_A1.GPIO_14, R1.Pin_0, S1.leg1
  N4: Raspberry_Pi_A1.GPIO_15, LED1.anode
  N5: Raspberry_Pi_A1.GPIO_18, S2.leg1, R2.Pin_0
  N6: Raspberry_Pi_A1.GPIO_24, S3.leg1, R3.Pin_0
  N7: Raspberry_Pi_A1.GPIO_25, LED3.anode
